# Fritzing sketch Arduino_LDRs_DHT (saved by Fritzing 0.9.3b)
breadboards: 1

parts:
  Part1 = Arduino Uno (Rev3)
  DHT1 = DHT11 Humitidy and Temperature Sensor
  R1 = Photocell (LDR) [package=THT]
  R2 = Photocell (LDR) [package=THT]
  T1 = LM35 Temperature Sensor [package="TO92 [THT]"]
  R3 = Resistor [tolerance=±5% resistance=220 package="0805 [SMD]"]
  R4 = Resistor [tolerance=±5% resistance=680 package=THT]
  R5 = Resistor [tolerance=±5% resistance=680 package=THT]

nets:
  N1: Part1.A0, R1.pin_0, R4.Pin_1
  N2: Part1.A1, T1.Vout
  N3: Part1.A2, R2.pin_0, R5.Pin_1
  N4: Part1.D2, DHT1.DATA, R3.Pin_1
  N5: DHT1.VDD, R1.pin_1, R2.pin_1, T1.+Vs, R3.Pin_0
  GND: DHT1.GND, T1.GND, R4.Pin_0, R5.Pin_0

custom parts:
  DHT11 Humitidy and Temperature Sensor: DHT11 Humidity and Temperature Sensor
  Photocell (LDR): A generic light dependent resistor (LDR)
